// Logisim project main.circ as structural Verilog: 5 circuits, main circuit main
module main (
);

  wire button_1_out, button_2_out, clock_1_out, controlador_auto_1_out_4, controlador_auto_1_out_5,
       controlador_auto_1_out_7, controlador_auto_1_verde, controlador_digitos_1_out_3,
       controlador_digitos_1_out_4, controlador_digitos_1_out_5, controlador_digitos_1_out_6,
       controlador_digitos_1_out_7, controlador_digitos_1_out_8, controlador_digitos_1_out_9,
       controlador_digitos_1_out_10, controlador_digitos_1_out_11, controlador_digitos_1_out_12,
       controlador_digitos_1_out_13, controlador_digitos_1_out_14, controlador_digitos_1_out_15,
       controlador_digitos_1_out_16, controlador_peaton_1_filtro, controlador_peaton_1_rojo,
       controlador_peaton_1_verde, filtro_1_out_3, not_1_out, or_1_out, or_2_out, or_3_out, or_4_out,
       or_5_out;

  Button button_1 (.out(button_1_out));
  not not_1 (not_1_out, button_1_out);
  Button button_2 (.out(button_2_out));
  Clock clock_1 (.out(clock_1_out));
  filtro filtro_1 (.Boton_Peatones(button_2_out), .in_2(controlador_peaton_1_filtro), .out_3(filtro_1_out_3));
  controlador_auto controlador_auto_1 (
    .Clock(clock_1_out), .Reset(not_1_out), .in_3(filtro_1_out_3), .out_4(controlador_auto_1_out_4),
    .out_5(controlador_auto_1_out_5), .Verde(controlador_auto_1_verde), .out_7(controlador_auto_1_out_7));
  controlador_peaton controlador_peaton_1 (
    .Clock(clock_1_out), .Reset(not_1_out), .Ctrl___Auto(controlador_auto_1_out_7),
    .Rojo(controlador_peaton_1_rojo), .Verde(controlador_peaton_1_verde), .Filtro(controlador_peaton_1_filtro));
  or or_1 (or_1_out, button_1_out, controlador_auto_1_out_4);
  or or_2 (or_2_out, button_1_out, controlador_auto_1_out_5);
  or or_3 (or_3_out, button_1_out, controlador_auto_1_verde);
  or or_4 (or_4_out, button_1_out, controlador_peaton_1_rojo);
  or or_5 (or_5_out, button_1_out, controlador_peaton_1_verde);
  controlador_digitos controlador_digitos_1 (
    .Clock(clock_1_out), .Ctrl_Auto(controlador_auto_1_out_7), .out_3(controlador_digitos_1_out_3),
    .out_4(controlador_digitos_1_out_4), .out_5(controlador_digitos_1_out_5),
    .out_6(controlador_digitos_1_out_6), .out_7(controlador_digitos_1_out_7),
    .out_8(controlador_digitos_1_out_8), .out_9(controlador_digitos_1_out_9),
    .out_10(controlador_digitos_1_out_10), .out_11(controlador_digitos_1_out_11),
    .out_12(controlador_digitos_1_out_12), .out_13(controlador_digitos_1_out_13),
    .out_14(controlador_digitos_1_out_14), .out_15(controlador_digitos_1_out_15),
    .out_16(controlador_digitos_1_out_16));
  LED led_1 (.in(or_1_out));
  LED led_2 (.in(or_2_out));
  LED led_3 (.in(or_3_out));
  LED led_4 (.in(or_4_out));
  LED led_5 (.in(or_5_out));
  _7_Segment_Display u_7_segment_display_1 (
    .g(controlador_digitos_1_out_6), .f(controlador_digitos_1_out_5), .a(controlador_digitos_1_out_4),
    .b(controlador_digitos_1_out_3), .e(controlador_digitos_1_out_7), .d(controlador_digitos_1_out_8),
    .c(controlador_digitos_1_out_9));  // open: dp
  _7_Segment_Display u_7_segment_display_2 (
    .g(controlador_digitos_1_out_13), .f(controlador_digitos_1_out_12), .a(controlador_digitos_1_out_11),
    .b(controlador_digitos_1_out_10), .e(controlador_digitos_1_out_14), .d(controlador_digitos_1_out_15),
    .c(controlador_digitos_1_out_16));  // open: dp

  // Notes on the sheet:
  //   Reset
  //   Boton Peaton
  //   ROJO AUTO
  //   AMARILLO AUTO
  //   VERDE AUTO
  //   ROJO PEATON
  //   VERDE PEATON
endmodule

// auto
module controlador_auto (
  input  Clock,
  input  Reset,
  input  in_3,
  output out_4,
  output out_5,
  output Verde,
  output out_7
);

  or or_1 (out_7, Clock, Reset, in_3);
  not not_1 (out_4, out_7);
  not not_2 (out_5, out_7);

  assign Verde = out_7;

  // Notes on the sheet:
  //   Boton - Peaton
  //   Controlador Peaton
  //   Rojo
  //   Amarillo
endmodule

// peaton
module controlador_peaton (
  input  Clock,
  input  Reset,
  input  Ctrl___Auto,
  output Rojo,
  output Verde,
  output Filtro
);

  wire or_1_out;

  buf or_1 (or_1_out, Ctrl___Auto);  // OR_Gate
  or or_2 (Filtro, Clock, Reset, or_1_out);
  not not_1 (Verde, Filtro);

  assign Rojo = Filtro;
endmodule

module controlador_digitos (
  input  Clock,
  input  Ctrl_Auto,
  output out_3,
  output out_4,
  output out_5,
  output out_6,
  output out_7,
  output out_8,
  output out_9,
  output out_10,
  output out_11,
  output out_12,
  output out_13,
  output out_14,
  output out_15,
  output out_16
);

  or or_1 (out_3, Clock, Ctrl_Auto);
  not not_1 (out_7, out_3);

  assign out_4 = out_3;
  assign out_5 = out_3;
  assign out_6 = out_3;
  assign out_8 = out_7;
  assign out_9 = out_3;
  assign out_10 = out_3;
  assign out_11 = out_3;
  assign out_12 = out_3;
  assign out_13 = out_3;
  assign out_14 = out_3;
  assign out_15 = out_3;
  assign out_16 = out_3;
endmodule

module filtro (
  input  Boton_Peatones,
  input  in_2,
  output out_3
);

  nor nor_1 (out_3, Boton_Peatones, in_2);

  // Notes on the sheet:
  //   Ctrl Peaton
endmodule
